# Fritzing sketch AudibleFlora (saved by Fritzing 0.9.3b)
breadboards: 1

parts:
  R1 = Resistor [tolerance=±5% resistance=470 package=THT]
  R2 = Resistor [tolerance=±5% resistance=470 package=THT]
  C1 = Ceramic Capacitor [capacitance=220nF package="100 mil [THT, multilayer]"]
  S1 = Pushbutton [package="[THT]"]
  R4 = Resistor [tolerance=±5% resistance=12k package=THT]
  Part2 = Arduino Pro Mini v13
  R3 = Resistor [tolerance=±5% resistance=270 package=THT]
  SPKR1 = Loudspeaker
  hc-sr2 = hc-sr04

nets:
  N1: R1.Pin_0, R2.Pin_1, Part2.D4
  N2: R1.Pin_1, hc-sr2.Echo
  GND: R2.Pin_0, C1.0, R4.Pin_0, Part2.GND, SPKR1.pin1, hc-sr2.GND
  N3: C1.1, R3.Pin_1, SPKR1.pin2
  N4: S1.Pin_1, S1.Pin_2, R4.Pin_1, Part2.D3_PWM
  5V: S1.Pin_3, S1.Pin_4, Part2.VCC, hc-sr2.VCC
  N5: Part2.D9_PWM, R3.Pin_0
  N6: Part2.D2, hc-sr2.Trig

custom parts:
  hc-sr04: This is a HC-SR04 Distance Sensor
